// Logisim project regfile.circ as structural Verilog: 1 circuit, main circuit regfile
module regfile (
  input  [4:0] ReadIndex1,
  input  [4:0] ReadIndex2,
  input  [4:0] WriteIndex,
  input  [31:0] WriteData,
  input  RegWEn,
  input  clk,
  output [31:0] ra,
  output [31:0] sp,
  output [31:0] t0,
  output [31:0] t1,
  output [31:0] t2,
  output [31:0] s0,
  output [31:0] s1,
  output [31:0] a0,
  output [31:0] ReadData1,
  output [31:0] ReadData2
);

  wire a0WEn, demultiplexer_1_out1, demultiplexer_1_out2, demultiplexer_1_out5, demultiplexer_1_out6,
       demultiplexer_1_out7, demultiplexer_1_out8, demultiplexer_1_out9, demultiplexer_1_out10, raWEn, s0WEn,
       s1WEn, spWEn, t0WEn, t1WEn, t2WEn;

  Register #(.width(32)) register_1 (.D(WriteData), .en(raWEn), .clk(clk), .Q(ra));  // open: clr
  Register #(.width(32)) register_2 (.D(WriteData), .en(t0WEn), .clk(clk), .Q(t0));  // open: clr
  Register #(.width(32)) register_3 (.D(WriteData), .en(t2WEn), .clk(clk), .Q(t2));  // open: clr
  Register #(.width(32)) register_4 (.D(WriteData), .en(s1WEn), .clk(clk), .Q(s1));  // open: clr
  Register #(.width(32)) register_5 (.D(WriteData), .en(spWEn), .clk(clk), .Q(sp));  // open: clr
  Register #(.width(32)) register_6 (.D(WriteData), .en(t1WEn), .clk(clk), .Q(t1));  // open: clr
  Register #(.width(32)) register_7 (.D(WriteData), .en(s0WEn), .clk(clk), .Q(s0));  // open: clr
  Register #(.width(32)) register_8 (.D(WriteData), .en(a0WEn), .clk(clk), .Q(a0));  // open: clr
  Multiplexer #(.select(5), .width(32)) multiplexer_1 (
    .in0({32{1'b0}}), .in1(ra), .in2(sp), .in5(t0), .in6(t1), .in7(t2), .in8(s0), .in9(s1), .in10(a0),
    .out(ReadData1), .sel(ReadIndex1));  // open: in3, in4, in11, in12, in13, in14, in15, in16, in17, in18, in19, in20, in21, in22, in23, in24, in25, in26, in27, in28, in29, in30, in31
  Demultiplexer #(.select(5)) demultiplexer_1 (
    .out1(demultiplexer_1_out1), .out2(demultiplexer_1_out2), .out5(demultiplexer_1_out5),
    .out6(demultiplexer_1_out6), .out7(demultiplexer_1_out7), .out8(demultiplexer_1_out8),
    .out9(demultiplexer_1_out9), .out10(demultiplexer_1_out10), .in(1'b1), .sel(WriteIndex));  // open: out0, out3, out4, out11, out12, out13, out14, out15, out16, out17, out18, out19, out20, out21, out22, out23, out24, out25, out26, out27, out28, out29, out30, out31
  and and_1 (raWEn, RegWEn, demultiplexer_1_out1);
  and and_2 (spWEn, RegWEn, demultiplexer_1_out2);
  and and_3 (t0WEn, RegWEn, demultiplexer_1_out5);
  and and_4 (t1WEn, RegWEn, demultiplexer_1_out6);
  and and_5 (t2WEn, demultiplexer_1_out7, RegWEn);
  and and_6 (s0WEn, demultiplexer_1_out8, RegWEn);
  and and_7 (s1WEn, demultiplexer_1_out9, RegWEn);
  and and_8 (a0WEn, demultiplexer_1_out10, RegWEn);
  Multiplexer #(.select(5), .width(32)) multiplexer_2 (
    .in0({32{1'b0}}), .in1(ra), .in2(sp), .in5(t0), .in6(t1), .in7(t2), .in8(s0), .in9(s1), .in10(a0),
    .out(ReadData2), .sel(ReadIndex2));  // open: in3, in4, in11, in12, in13, in14, in15, in16, in17, in18, in19, in20, in21, in22, in23, in24, in25, in26, in27, in28, in29, in30, in31

  // Notes on the sheet:
  //   INPUTS to your circuit
  //   DON'T CHANGE THE LOCATIONS OF THE INPUTS AND OUTPUTS!
  //   These are DEBUG/TEST outputs from your circuit.
  //   OUTPUTS from your circuit
endmodule
